# Fritzing sketch schema (saved by Fritzing 0.9.6b)

parts:
  MPU-6050 = MPU-6050 Board GY-521 [form="♀ (female)" package=THT]
  Arduino_Nano = Arduino Nano (Rev3.0)
  Buzzer_5V = Piezo Buzzer
  Transistor_2N2222_-_BC547 = PNP-Transistor [package="TO92 [THT]"]
  C2 = Ceramic Capacitor [capacitance="100 nF" voltage=35V package="1206 [SMD, multilayer]"]
  R1 = Resistor [tolerance=±5% resistance=6.8k package="0402 [SMD]"]
  500_mAh_LiPo_(11_1V) = LiPoly Battery (1300mAh)
  R7 = Resistor [tolerance=±5% power=0.25 resistance=33k package=THT]
  R8 = Resistor [tolerance=±5% power=0.25 resistance=22k package=THT]
  Nidec_24H404H160 = double row male pin header, 8 pins [form="♂ (male)"]

nets:
  N1: MPU-6050.pin2, Transistor_2N2222_-_BC547.C, 500_mAh_LiPo_(11_1V).negative
  N2: MPU-6050.pin3, Arduino_Nano.A5
  N3: MPU-6050.pin4, Arduino_Nano.A4
  N4: Arduino_Nano.D4, Nidec_24H404H160.pin5
  N5: Arduino_Nano.D8, Nidec_24H404H160.pin3
  N6: Arduino_Nano.D9, Nidec_24H404H160.pin4
  N7: Arduino_Nano.D12/MISO, R1.Pin_1
  N8: Arduino_Nano.VIN, 500_mAh_LiPo_(11_1V).positive, R7.Pin_0
  N9: Arduino_Nano.5V, Buzzer_5V.pin_1
  N10: Arduino_Nano.A7, C2.1, R7.Pin_1, R8.Pin_0
  N11: Buzzer_5V.pin_2, Transistor_2N2222_-_BC547.E
  N12: Transistor_2N2222_-_BC547.B, R1.Pin_0
  N13: C2.0, R8.Pin_1

custom parts:
  MPU-6050 Board GY-521: Acelerometro y Giroscopio MPU-6050 Board GY-521
  Piezo Buzzer: Part from https://www.nutsvolts.com/magazine/article/november2012_SmileysWorkshop modified to be .3 in spacing to match the adafruit buzzer 5V breadboard friendly part.
  LiPoly Battery (1300mAh): Lithium Ion Polymer Battery (1300mAh)
