# Fritzing sketch schema_breadboard (saved by Fritzing 0.9.6b)
breadboards: 1

parts:
  J1 = Camdenboss CTB0158-2 [part_number=CTB0158-2 package=THT]
  500_mAh_LiPo_(11_1V)1 = LiPoly Battery (1300mAh)
  Arduino_Nano1 = Arduino Nano (Rev3.0)
  S3 = SPST Switch [package=switch-spdt_kit]
  R9 = Resistor [tolerance=±5% power=0.25 resistance=33k package=THT]
  C3 = Ceramic Capacitor [capacitance="100 nF" voltage=35V package="1206 [SMD, multilayer]"]
  R10 = Resistor [tolerance=±5% power=0.25 resistance=22k package=THT]
  MPU-6051 = MPU-6050 Board GY-521 [form="♀ (female)" package=THT]
  Buzzer_5V1 = Piezo Buzzer
  Transistor_2N2222_-_BC548 = PNP-Transistor [package="TO92 [THT]"]
  R11 = Resistor [tolerance=±5% resistance=6.8k package="0402 [SMD]"]
  Nidec_24H404H161 = double row male pin header, 8 pins [form="♂ (male)"]

nets:
  N1: J1.pin1, Arduino_Nano1.VIN, R9.Pin_1, Nidec_24H404H161.pin1
  N2: J1.pin2, Arduino_Nano1.GND, C3.1, R10.Pin_0, MPU-6051.pin2, Transistor_2N2222_-_BC548.C, Nidec_24H404H161.pin2
  N3: J1.terminal_1, S3.O
  N4: J1.terminal_2, 500_mAh_LiPo_(11_1V)1.negative
  N5: 500_mAh_LiPo_(11_1V)1.positive, S3.S
  N6: Arduino_Nano1.D4, Nidec_24H404H161.pin5
  N7: Arduino_Nano1.D8, Nidec_24H404H161.pin3
  N8: Arduino_Nano1.D9, Nidec_24H404H161.pin4
  N9: Arduino_Nano1.D12/MISO, R11.Pin_0
  N10: Arduino_Nano1.5V, MPU-6051.pin1, Buzzer_5V1.pin_1
  N11: Arduino_Nano1.A7, R9.Pin_0, C3.0, R10.Pin_1
  N12: Arduino_Nano1.A5, MPU-6051.pin3
  N13: Arduino_Nano1.A4, MPU-6051.pin4
  N14: Buzzer_5V1.pin_2, Transistor_2N2222_-_BC548.E
  N15: Transistor_2N2222_-_BC548.B, R11.Pin_1

custom parts:
  LiPoly Battery (1300mAh): Lithium Ion Polymer Battery (1300mAh)
  MPU-6050 Board GY-521: Acelerometro y Giroscopio MPU-6050 Board GY-521
  Piezo Buzzer: Part from https://www.nutsvolts.com/magazine/article/november2012_SmileysWorkshop modified to be .3 in spacing to match the adafruit buzzer 5V breadboard friendly part.
